# Fritzing sketch LDRPiezoSpeakerUno5V (saved by Fritzing 0.9.2b)
breadboards: 1

parts:
  Piezo_Speaker = Piezo Speaker
  BC337 = TRANSISTOR_NPN_2 [package=to-92]
  part = Resistor [tolerance=±5% resistance=1k package="1206 [SMD]"]
  D2 = Rectifier Diode [package="Melf DO-213 AA [SMD]"]
  Part1 = Arduino Uno (Rev3) - ICSP
  5V = Power plug
  R2 = Photocell (LDR) [package=THT]
  R3 = Resistor [tolerance=±5% resistance=10k package="0805 [SMD]"]

nets:
  N1: Piezo_Speaker.pin1, BC337.C, D2.anode
  5V: Piezo_Speaker.pin2, D2.cathode, Part1.5V, 5V.VCC, R2.pin_1
  N2: BC337.B, part.Pin_0
  GND: BC337.E, Part1.GND, 5V.GND, R3.Pin_0
  N3: part.Pin_1, Part1.D3_PWM
  N4: Part1.A0, R2.pin_0, R3.Pin_1
